# Fritzing sketch tuto-11 (saved by Fritzing 0.9.3b)

parts:
  Part1 = Arduino Uno (Rev3)
  LCD1 = LCD screen
  R1 = Rotary Potentiometer (Small) [maximum_resistance=100kΩ package=THT]

nets:
  N1: Part1.D11_PWM/MOSI, LCD1.E
  N2: Part1.D12/MISO, LCD1.RS
  N3: Part1.D2, LCD1.DB7
  N4: Part1.D3_PWM, LCD1.DB6
  N5: Part1.D4, LCD1.DB5
  N6: Part1.D5_PWM, LCD1.DB4
  5V: Part1.5V, LCD1.VDD, R1.leg1
  GND: Part1.GND, LCD1.VSS, LCD1.R/W, R1.leg2
  N7: LCD1.V0, R1.wiper

notes:
  D5
  D7
  D6
  D4
  RS
  E
  R/W
  VSS
  VDD
  V0
