# Fritzing sketch tuto-12 (saved by Fritzing 0.9.3b)

parts:
  Composant1 = Arduino Uno (Rev3)
  Disp2 = LBT2088AH [part_number=LBT2088AH]

nets:
  N1: Composant1.A0, Disp2.pin_9
  N2: Composant1.A1, Disp2.pin_7
  N3: Composant1.A2, Disp2.pin2
  N4: Composant1.A3, Disp2.pin_5
  N5: Composant1.D8, Disp2.pin_15
  N6: Composant1.D9_PWM, Disp2.pin_16
  N7: Composant1.D10_PWM/SS, Disp2.pin_14
  N8: Composant1.D11_PWM/MOSI, Disp2.pin_8
  N9: Composant1.D12/MISO, Disp2.pin_12
  N10: Composant1.D13/SCK, Disp2.pin1
  N11: Composant1.D2, Disp2.pin_13
  N12: Composant1.D3_PWM, Disp2.pin_3
  N13: Composant1.D4, Disp2.pin_4
  N14: Composant1.D5_PWM, Disp2.pin_10
  N15: Composant1.D6_PWM, Disp2.pin_6
  N16: Composant1.D7, Disp2.pin_11

notes:
  Coté encoche
