# Fritzing sketch tuto-5 (saved by Fritzing 0.9.3b)
breadboards: 1

parts:
  Composant1 = Arduino Uno (Rev3)
  MIC1 = Microphone

nets:
  N1: Composant1.D10_PWM/SS, MIC1.pin2
  N2: Composant1.GND, MIC1.pin1
