# Fritzing sketch tuto-6 (saved by Fritzing 0.9.3b)
breadboards: 1

parts:
  Composant1 = Arduino Uno (Rev3)
  LED1 = LED - 5mm [color="Red (633nm)" package="5 mm [THT]"]
  R1 = Resistor [tolerance=±5% resistance=330 package=THT]
  R2 = Resistor [tolerance=±5% resistance=10k package=THT]
  R3 = Photocell (LDR) [package=THT]

nets:
  N1: Composant1.A2, R2.Pin_0, R3.pin_1
  N2: Composant1.GND, LED1.cathode, R2.Pin_1
  N3: Composant1.D4, R1.Pin_1
  N4: Composant1.5V, R3.pin_0
  N5: LED1.anode, R1.Pin_0
