# Fritzing sketch tuto-8 (saved by Fritzing 0.9.3b)
breadboards: 1

parts:
  Composant1 = Arduino Uno (Rev3)
  RHT1 = Humidity and Temperature Sensor RHT03
  R1 = Resistor [tolerance=±5% resistance=220 package=THT]

nets:
  N1: Composant1.GND, RHT1.GND_2
  N2: Composant1.D4, RHT1.Data-signal, R1.Pin_1
  5V: Composant1.5V, RHT1.Vcc, R1.Pin_0
